# Fritzing sketch schema (saved by Fritzing 0.6.3b)
breadboards: 1

parts:
  Arduino1 = Arduino
  LED1 = LED - 5mm [color="Red (633nm)" package="5 mm [THT]"]
  LED2 = LED - 5mm [color="Red (633nm)" package="5 mm [THT]"]

nets:
  N1: Arduino1.D12, LED1.cathode
  N2: Arduino1.D11, LED2.cathode
  N3: Arduino1.GND, LED1.anode, LED2.anode
